# Fritzing sketch wiring (saved by Fritzing 0.9.0b)
breadboards: 1

parts:
  IC3 = A7105 [chip_label=IC package="DIP (Dual Inline) [THT]"]
  Bauteil1 = Arduino Pro Mini v13
  Bauteil2 = Arduino Pro Mini v13
  S1 = Pushbutton [package="[THT]"]
  LED1 = LED - 5mm [color="Green (555nm)" package="5 mm [THT]"]
  LED2 = LED - 5mm [color="Red (633nm)" package="5 mm [THT]"]
  R1 = Resistor [tolerance=±5% resistance=220 package=THT]
  R2 = Resistor [tolerance=±5% resistance=220 package=THT]

nets:
  N1: IC3.pin1, IC3.pin10, Bauteil1.A1, Bauteil2.GND, S1.Pin_1, S1.Pin_2, LED1.anode, LED2.anode
  N2: IC3.pin6, Bauteil2.D12/MISO
  N3: IC3.pin9, Bauteil2.VCC
  N4: IC3.pin12, Bauteil2.D10_PWM/SS
  N5: IC3.pin13, Bauteil2.D13/SCK
  N6: IC3.pin14, Bauteil2.D11_PWM/MOSI
  N7: Bauteil1.A0, LED2.cathode, R2.Pin_1
  N8: Bauteil1.D10_PWM/SS, Bauteil2.D9_PWM, R2.Pin_0
  N9: Bauteil2.RESET, S1.Pin_3, S1.Pin_4
  N10: Bauteil2.D8, R1.Pin_0
  N11: LED1.cathode, R1.Pin_1

custom parts:
  A7105: A DIP stand-in part for whatever IC you want. With 14 pins on a 300mil dual inline package (DIP) footprint.
